# Fritzing sketch Shift Register (saved by Fritzing 0.9.3b)
breadboards: 1

parts:
  U1 = NodeMCU V3.0
  U2 = 74HC595 SMD [package="SO16 [SMD]"]
  LED2 = LED - 5mm [color="Red (633nm)" package="5 mm [THT]"]
  LED3 = LED - 5mm [color="Red (633nm)" package="5 mm [THT]"]
  LED4 = LED - 5mm [color="Red (633nm)" package="5 mm [THT]"]
  LED5 = LED - 5mm [color="Red (633nm)" package="5 mm [THT]"]
  LED6 = LED - 5mm [color="Red (633nm)" package="5 mm [THT]"]
  LED7 = LED - 5mm [color="Red (633nm)" package="5 mm [THT]"]
  LED8 = LED - 5mm [color="Red (633nm)" package="5 mm [THT]"]
  LED9 = LED - 5mm [color="Red (633nm)" package="5 mm [THT]"]
  R1 = Resistor [tolerance=±5% resistance=220 package="2512 [SMD]"]
  R2 = Resistor [tolerance=±5% resistance=220 package="2512 [SMD]"]
  R3 = Resistor [tolerance=±5% resistance=220 package="2512 [SMD]"]
  R4 = Resistor [tolerance=±5% resistance=220 package="2512 [SMD]"]
  R5 = Resistor [tolerance=±5% resistance=220 package="2512 [SMD]"]
  R6 = Resistor [tolerance=±5% resistance=220 package="2512 [SMD]"]
  R7 = Resistor [tolerance=±5% resistance=220 package="2512 [SMD]"]
  R8 = Resistor [tolerance=±5% resistance=220 package="2512 [SMD]"]

nets:
  3V3: U1.3V3, U2.MR, U2.VCC
  GND: U1.GND, U2.GND, LED2.anode, LED3.anode, LED4.anode, LED5.anode, LED6.anode, LED7.anode, LED8.anode, LED9.anode
  N1: U1.D5, U2.SH_CP
  N2: U1.D6, U2.OE
  N3: U1.D7, U2.DS
  N4: U1.D8, U2.ST_CP
  N5: U2.Q1, R8.Pin_0
  N6: U2.Q2, R7.Pin_0
  N7: U2.Q3, R5.Pin_0
  N8: U2.Q4, R6.Pin_0
  N9: U2.Q5, R4.Pin_0
  N10: U2.Q6, R3.Pin_0
  N11: U2.Q7, R2.Pin_0
  N12: U2.Q0, R1.Pin_0
  N13: LED2.cathode, R2.Pin_1
  N14: LED3.cathode, R3.Pin_1
  N15: LED4.cathode, R4.Pin_1
  N16: LED5.cathode, R6.Pin_1
  N17: LED6.cathode, R5.Pin_1
  N18: LED7.cathode, R7.Pin_1
  N19: LED8.cathode, R8.Pin_1
  N20: LED9.cathode, R1.Pin_1

custom parts:
  NodeMCU V3.0: ESP8266 based NodeMCU
