# Fritzing sketch Shift Register_v2 (saved by Fritzing 0.9.3b)
circuit board: 9.2cm x 7.4cm
breadboards: 1

parts:
  U1 = NodeMCU V3.0
  J1 = Camdenboss CTB0158-2 [part_number=CTB0158-2 package=THT]
  J2 = Camdenboss CTB0158-2 [part_number=CTB0158-2 package=THT]
  J3 = Camdenboss CTB0158-2 [part_number=CTB0158-2 package=THT]
  J4 = Camdenboss CTB0158-2 [part_number=CTB0158-2 package=THT]
  J5 = Camdenboss CTB0158-2 [part_number=CTB0158-2 package=THT]
  J8 = Camdenboss CTB0158-2 [part_number=CTB0158-2 package=THT]
  J13 = Camdenboss CTB0158-2 [part_number=CTB0158-2 package=THT]
  J14 = Camdenboss CTB0158-2 [part_number=CTB0158-2 package=THT]
  U3 = 74HC595 [package="DIP16 [THT]"]
  R3 = Resistor [tolerance=±5% resistance=220 package=THT]
  R6 = Resistor [tolerance=±5% resistance=220 package=THT]
  R4 = Resistor [tolerance=±5% resistance=220 package=THT]
  R2 = Resistor [tolerance=±5% resistance=220 package=THT]
  R5 = Resistor [tolerance=±5% resistance=220 package=THT]
  R1 = Resistor [tolerance=±5% resistance=220 package=THT]
  R8 = Resistor [tolerance=±5% resistance=220 package=THT]
  R7 = Resistor [tolerance=±5% resistance=220 package=THT]

nets:
  3V3: U1.3V3, U3.MR, U3.VCC
  GND: U1.GND, J1.pin2, J2.pin2, J3.pin2, J4.pin2, J5.pin2, J8.pin2, J13.pin2, J14.pin2, U3.GND
  N1: U1.D5, U3.SH_CP
  N2: U1.D6, U3.OE
  N3: U1.D7, U3.DS
  N4: U1.D8, U3.ST_CP
  N5: J1.pin1, R8.Pin_0
  N6: J2.pin1, R5.Pin_0
  N7: J3.pin1, R1.Pin_0
  N8: J4.pin1, R2.Pin_1
  N9: J5.pin1, R7.Pin_0
  N10: J8.pin1, R6.Pin_1
  N11: J13.pin1, R4.Pin_1
  N12: J14.pin1, R3.Pin_0
  N13: U3.Q1, R4.Pin_0
  N14: U3.Q2, R2.Pin_0
  N15: U3.Q3, R6.Pin_0
  N16: U3.Q4, R5.Pin_1
  N17: U3.Q5, R1.Pin_1
  N18: U3.Q6, R7.Pin_1
  N19: U3.Q7, R8.Pin_1
  N20: U3.Q0, R3.Pin_1

custom parts:
  NodeMCU V3.0: ESP8266 based NodeMCU
